# Fritzing sketch Les2 (saved by Fritzing 0.9.4)
breadboards: 2

parts:
  Onderdeel1 = Arduino Uno (Rev3)
  Onderdeel2 = Arduino Uno (Rev3)
  R1 = Resistor [tolerance=±5% resistance=220 package=THT]
  LED1 = LED - 5mm [color="Red (633nm)" package="5 mm [THT]"]
  R2 = Resistor [tolerance=±5% resistance=220 package=THT]  # not connected
  LED2 = LED - 5mm [color="Red (633nm)" package="5 mm [THT]"]

nets:
  N1: Onderdeel1.GND, LED1.cathode
  N2: Onderdeel2.GND, LED2.cathode
  N3: Onderdeel2.D3_PWM, R1.Pin_0
  N4: R1.Pin_1, LED1.anode
